// Logisim project LAB-2.circ as structural Verilog: 1 circuit, main circuit main
module main (
  input  in_1,
  input  in_2,
  input  in_3,
  input  in_4,
  input  in_5,
  input  in_6,
  input  in_7,
  input  in_8,
  input  in_9,
  input  in_10,
  input  in_11,
  input  in_12,
  input  in_13,
  input  in_14,
  input  in_15,
  input  in_16,
  output out_17,
  output out_18,
  output out_19,
  output out_20,
  output out_21,
  output out_22,
  output out_23
);

  wire and_1_out, and_2_out, and_3_out, nand_1_out, nand_2_out, nand_3_out, nand_4_out, nand_5_out,
       nand_6_out, nand_7_out, nand_9_out, nand_10_out, nand_11_out, nand_12_out, nand_15_out, nand_16_out,
       nand_17_out, nand_18_out, nand_19_out, nand_20_out, nand_21_out, not_1_out, not_2_out, not_3_out,
       not_4_out, not_5_out, or_1_out, undriven, undriven_2, undriven_3, undriven_4, undriven_5, undriven_6,
       undriven_7;

  not not_1 (not_1_out, undriven);
  not not_2 (not_2_out, undriven_2);
  and and_1 (and_1_out, in_1, in_1, in_2);
  or or_1 (or_1_out, in_4, in_6);
  nand nand_1 (nand_1_out, in_7, in_10);
  not not_3 (not_3_out, undriven_2);
  nand nand_2 (nand_2_out, in_7, nand_1_out);
  nand nand_3 (nand_3_out, nand_1_out, in_10);
  nand nand_4 (nand_4_out, undriven_4, undriven_3);
  and and_2 (and_2_out, not_1_out, undriven_2, undriven_2);
  nand nand_5 (nand_5_out, undriven_2, undriven);
  and and_3 (and_3_out, undriven, not_2_out, not_3_out);
  not not_4 (not_4_out, and_1_out);
  not not_5 (not_5_out, or_1_out);
  nand nand_6 (nand_6_out, nand_4_out, undriven_3);
  nand nand_7 (nand_7_out, undriven_4, nand_4_out);
  nand nand_8 (out_18, nand_2_out, nand_3_out);
  nand nand_9 (nand_9_out, undriven_5, nand_7_out, nand_6_out);
  not nand_10 (nand_10_out, nand_9_out);  // NAND_Gate
  not nand_11 (nand_11_out, nand_9_out);  // NAND_Gate
  nand nand_12 (nand_12_out, nand_10_out, in_13);
  or or_2 (out_23, and_2_out, and_2_out, nand_5_out, and_3_out);
  nand nand_13 (out_21, nand_11_out, nand_12_out, nand_12_out);
  nand nand_14 (out_22, nand_9_out, nand_4_out);
  nand nand_15 (nand_15_out, in_3, undriven_6);
  nand nand_16 (nand_16_out, undriven_7, in_9);
  nand nand_17 (nand_17_out, in_3, nand_15_out);
  nand nand_18 (nand_18_out, nand_15_out, undriven_6);
  nand nand_19 (nand_19_out, undriven_7, nand_16_out);
  nand nand_20 (nand_20_out, nand_16_out, in_9);
  nand nand_21 (nand_21_out, nand_17_out, nand_18_out, nand_18_out);
  nand nand_22 (out_19, nand_19_out, nand_19_out, nand_20_out);
  nand nand_23 (out_20, nand_16_out, nand_16_out);
  nor nor_1 (out_17, nand_21_out, nand_21_out);
endmodule
