// Logisim project LAB_19_09_2023.circ as structural Verilog: 1 circuit, main circuit main
module main (
  input  in_1,
  input  in_2,
  input  in_3,
  input  in_4,
  input  in_5,
  input  in_6,
  input  in_7,
  input  in_8,
  input  in_9,
  input  in_10,
  input  in_11,
  input  in_12,
  input  in_13,
  input  in_14,
  input  in_15,
  input  in_16,
  input  in_17,
  input  in_18,
  input  in_19
);

  wire and_1_out, and_2_out, and_3_out, and_4_out, and_5_out, and_6_out, and_7_out, and_8_out, nand_1_out,
       nor_1_out, not_1_out, not_2_out, not_3_out, or_1_out, or_2_out, or_3_out, undriven, xnor_1_out,
       xor_1_out, xor_2_out, xor_3_out, xor_4_out, xor_5_out, xor_6_out;

  not not_1 (not_1_out, in_4);
  not not_2 (not_2_out, in_5);
  and and_1 (and_1_out, not_1_out, in_5, in_6);
  and and_2 (and_2_out, not_1_out, not_2_out, not_3_out);
  and and_3 (and_3_out, in_4, not_2_out, in_6);
  not not_3 (not_3_out, in_6);
  and and_4 (and_4_out, in_17, in_18);
  xor xor_1 (xor_1_out, in_3, in_7);
  xnor xnor_1 (xnor_1_out, in_8, in_9);
  nand nand_1 (nand_1_out, undriven, in_11);
  nor nor_1 (nor_1_out, in_14, in_15);
  LED led_1 (.in(xor_1_out));
  LED led_2 (.in(xnor_1_out));
  LED led_3 (.in(nand_1_out));
  LED led_4 (.in(nor_1_out));
  xor xor_2 (xor_2_out, in_17, in_18);
  or or_1 (or_1_out, and_4_out, and_5_out);
  LED led_5 (.in(or_2_out));
  or or_2 (or_2_out, and_1_out, and_1_out, and_2_out, and_3_out);
  and and_5 (and_5_out, xor_2_out, in_19);
  LED led_6 (.in(or_1_out));
  xor xor_3 (xor_3_out, in_1, in_2);
  and and_6 (and_6_out, in_13, in_12);
  xor xor_4 (xor_4_out, xor_2_out, in_19);
  LED led_7 (.in(xor_3_out));
  and and_7 (and_7_out, in_2, in_1);
  LED led_8 (.in(and_7_out));
  xor xor_5 (xor_5_out, in_12, in_13);
  or or_3 (or_3_out, and_6_out, and_8_out);
  LED led_9 (.in(xor_4_out));
  LED led_10 (.in(or_3_out));
  and and_8 (and_8_out, xor_5_out, in_16);
  xor xor_6 (xor_6_out, xor_5_out, in_16);
  LED led_11 (.in(xor_6_out));

  // Notes on the sheet:
  //   LOGIC GATES
  //   A^BC+A^B^C^+AB^C
  //   HALF ADDER
  //   FULL ADDER
endmodule
