// Logisim project Half Subtractor_26_09_23.circ as structural Verilog: 1 circuit, main circuit main
module main (
  input  in_1,
  input  in_2
);

  wire and_1_out, not_1_out, xor_1_out;

  xor xor_1 (xor_1_out, in_1, in_2);
  not not_1 (not_1_out, in_1);
  LED led_1 (.in(xor_1_out));
  and and_1 (and_1_out, not_1_out, in_2);
  LED led_2 (.in(and_1_out));

  // Notes on the sheet:
  //   Half subtractor Subtractor
  //   Difference
  //   Borrow
endmodule
