// Logisim project MUX.circ as structural Verilog: 1 circuit, main circuit main
module main (
  input  S1,
  input  S0,
  input  A3,
  input  A2,
  input  A1,
  input  A0,
  output out_7
);

  wire and_1_out, and_2_out, and_3_out, and_4_out, not_1_out, not_2_out;

  not not_1 (not_1_out, S1);
  not not_2 (not_2_out, S0);
  and and_1 (and_1_out, S1, S0, A3);
  and and_2 (and_2_out, S1, not_2_out, A2);
  and and_3 (and_3_out, not_1_out, S0, A1);
  and and_4 (and_4_out, not_1_out, not_2_out, A0);
  or or_1 (out_7, and_1_out, and_2_out, and_3_out, and_4_out);
endmodule
