// Logisim project full_sub_using_mux.circ as structural Verilog: 1 circuit, main circuit main
module main (
  input  in_1,
  input  in_2,
  input  in_3,
  input  in_4,
  input  in_5,
  input  in_6,
  input  in_7,
  input  in_8,
  input  [2:0] in_9,
  input  in_10,
  input  in_11,
  input  in_12,
  input  in_13,
  input  in_14
);

  wire multiplexer_1_out, multiplexer_2_out;

  Multiplexer #(.select(3)) multiplexer_1 (
    .in0(in_1), .in1(in_2), .in2(in_2), .in3(in_3), .in4(in_4), .in5(in_5), .in6(in_6), .in7(in_7),
    .out(multiplexer_1_out), .sel(in_9), .en(in_8));
  Multiplexer #(.select(3)) multiplexer_2 (
    .in0(in_10), .in1(in_11), .in2(in_11), .in3(in_12), .in4(in_13), .in5(in_13), .in6(in_13), .in7(in_14),
    .out(multiplexer_2_out), .sel(in_9), .en(in_8));
  LED led_1 (.in(multiplexer_1_out));
  LED led_2 (.in(multiplexer_2_out));
endmodule
