// Logisim project half_adder_using_mux.circ as structural Verilog: 1 circuit, main circuit main
module main (
  input  in_1,
  input  in_2,
  input  in_3,
  input  in_4,
  input  in_5,
  input  in_6,
  input  [1:0] in_7,
  input  in_8,
  input  in_9,
  input  in_10
);

  wire multiplexer_1_out, multiplexer_2_out;

  Multiplexer #(.select(2)) multiplexer_1 (
    .in0(in_1), .in1(in_2), .in2(in_3), .in3(in_4), .out(multiplexer_1_out), .sel(in_7), .en(in_5));
  Multiplexer #(.select(2)) multiplexer_2 (
    .in0(in_6), .in1(in_8), .in2(in_9), .in3(in_10), .out(multiplexer_2_out), .sel(in_7), .en(in_5));
  LED led_1 (.in(multiplexer_1_out));
  LED led_2 (.in(multiplexer_2_out));
endmodule
