// Logisim project Lab-4.circ as structural Verilog: 2 circuits, main circuit main
module main (
  input  [1:0] Write_register,
  input  [3:0] Write_data,
  input  [1:0] read_register_1,
  input  [1:0] read_register_2,
  input  reg_write,
  output [3:0] read_data_1,
  output [3:0] read_data_2
);

  wire clock_out;

  _4_bit_register u_4_bit_register_1 (
    .Write_Data(Write_register), .Write_data_2(Write_data), .reg_write(reg_write),
    .Read_register_1(read_register_1), .Read_register_2(read_register_2), .Read_data_1(read_data_1),
    .Read_data_2(read_data_2), .Clock(clock_out));
  Clock clock (.out(clock_out));
endmodule

module _4_bit_register (
  input  [3:0] Read_data_1,
  input  [3:0] Read_data_2,
  input  [1:0] Write_Data,
  input  [3:0] Write_data_2,
  input  Clock,
  input  reg_write,
  input  [1:0] Read_register_1,
  input  [1:0] Read_register_2
);

  wire and_1_out, and_2_out, and_3_out, and_4_out, decoder_1_out0, decoder_1_out1, decoder_1_out2,
       decoder_1_out3, undriven;
  wire [3:0] register_1_q, register_2_q, register_3_q, register_4_q;

  Decoder #(.select(2)) decoder_1 (
    .out0(decoder_1_out0), .out1(decoder_1_out1), .out2(decoder_1_out2), .out3(decoder_1_out3),
    .sel(Write_Data));  // open: en
  buf and_1 (and_1_out, undriven);  // AND_Gate
  and and_2 (and_2_out, decoder_1_out3, undriven);
  Register #(.width(4)) register_1 (.D(Write_data_2), .Q(register_1_q), .clk(Clock), .clr(and_1_out));  // open: en
  Register #(.width(4)) register_2 (.D(Write_data_2), .Q(register_2_q), .clk(Clock), .clr(and_2_out));  // open: en
  buf and_3 (and_3_out, undriven);  // AND_Gate
  and and_4 (and_4_out, decoder_1_out1, undriven);
  Register #(.width(4)) register_3 (.D(Write_data_2), .Q(register_3_q), .clk(Clock), .clr(and_3_out));  // open: en
  Register #(.width(4)) register_4 (.D(Write_data_2), .Q(register_4_q), .clk(Clock), .clr(and_4_out));  // open: en
  Multiplexer #(.select(2), .width(4)) multiplexer_1 (
    .in0(register_1_q), .in1(register_2_q), .in2(register_3_q), .in3(register_4_q), .out(Read_data_2),
    .sel(Read_register_2));  // open: en
  Multiplexer #(.select(2), .width(4)) multiplexer_2 (
    .in0(register_1_q), .in1(register_2_q), .in2(register_3_q), .in3(register_4_q), .out(Read_data_1),
    .sel(Read_register_1));  // open: en
endmodule
