// Digital circuit 4 bit ALU.dig as structural Verilog
module _4_bit_ALU (
  input  S_2,
  input  S_1,
  input  S_0,
  input  [3:0] A,
  input  [3:0] B,
  input  C_in,
  output [3:0] Y,
  output C_out
);

  wire [3:0] _4_bit_au_1_d, _4_bit_lu_1_f;

  _4_bit_AU _4_bit_au_1 (.A(A), .B(B), .C_in(C_in), .S_1(S_1), .S_0(S_0), .D(_4_bit_au_1_d), .C_out(C_out));
  _4_bit_LU _4_bit_lu_1 (.F(_4_bit_lu_1_f), .A(A), .B(B), .S_1(S_1), .S_0(S_0));
  Multiplexer #(.Bits(4)) multiplexer_1 (.sel(S_2), .in_0(_4_bit_au_1_d), .in_1(_4_bit_lu_1_f), .out(Y));
endmodule
