// Digital circuit 4-bit AU.dig as structural Verilog
module _4_bit_AU (
  input  [3:0] B,
  input  S_0,
  input  S_1,
  input  [3:0] A,
  input  C_in,
  output [3:0] D,
  output C_out
);

  wire [3:0] multiplexer_1_out, not_1_out, not_2_out;

  assign not_1_out = ~B;  // Not not_1, 4 bits wide
  assign not_2_out = ~4'b0000;  // Not not_2, 4 bits wide
  Multiplexer #(.Bits(4), .Selector_Bits(2)) multiplexer_1 (
    .sel({S_1, S_0}), .in_0(B), .in_1(not_1_out), .in_2(4'b0000), .in_3(not_2_out), .out(multiplexer_1_out));
  Add #(.Bits(4)) add_1 (.a(A), .b(multiplexer_1_out), .c_i(C_in), .s(D), .c_o(C_out));
endmodule
