// Digital circuit 4-bit LU.dig as structural Verilog
module _4_bit_LU (
  input  [3:0] A,
  input  [3:0] B,
  input  S_0,
  input  S_1,
  output [3:0] F
);

  wire [3:0] and_1_out, not_1_out, or_1_out, xor_1_out;

  assign and_1_out = A & B;  // And and_1, 4 bits wide
  assign or_1_out = A | B;  // Or or_1, 4 bits wide
  assign xor_1_out = A ^ B;  // XOr xor_1, 4 bits wide
  assign not_1_out = ~A;  // Not not_1, 4 bits wide
  Multiplexer #(.Selector_Bits(2), .Bits(4)) multiplexer_1 (
    .sel({S_1, S_0}), .in_0(and_1_out), .in_1(or_1_out), .in_2(xor_1_out), .in_3(not_1_out), .out(F));
endmodule
