// Logisim project LAB-4.circ as structural Verilog: 9 circuits, main circuit main
module main (
  input  in_1,
  input  [3:0] B,
  input  [3:0] A,
  input  S2,
  input  S1,
  input  S0,
  input  [3:0] Constant,
  output out_8,
  output [3:0] out_9,
  output out_10
);

  wire [3:0] au_4_bit_1_d, n4_bit_lu_1_out_5;

  AU_4_bit au_4_bit_1 (
    .A(A), .B(B), .Constant(Constant), .S1(S1), .C_IN(in_1), .D(au_4_bit_1_d), .Overflow(out_8),
    .CarryOut(out_10), .S0(S0));
  _4_bit_LU u_4_bit_lu_1 (.A(A), .B(B), .S0(S0), .S1(S1), .out_5(n4_bit_lu_1_out_5));
  Muti_Bit_Mux muti_bit_mux_1 (.A(au_4_bit_1_d), .B(n4_bit_lu_1_out_5), .Select(S2), .out_4(out_9));
endmodule

module FA (
  input  A,
  input  B,
  input  Cin,
  output SUM,
  output CARRY
);

  wire and_1_out, and_2_out, and_3_out, and_4_out, and_5_out, and_6_out, and_7_out, not_1_out, not_2_out,
       not_3_out, not_4_out, not_5_out, not_6_out;

  not not_1 (not_1_out, A);
  not not_2 (not_2_out, B);
  not not_3 (not_3_out, A);
  not not_4 (not_4_out, Cin);
  not not_5 (not_5_out, B);
  not not_6 (not_6_out, Cin);
  and and_1 (and_1_out, B, Cin);
  and and_2 (and_2_out, A, Cin);
  and and_3 (and_3_out, A, B);
  and and_4 (and_4_out, not_1_out, not_2_out, Cin);
  and and_5 (and_5_out, not_3_out, B, not_4_out);
  and and_6 (and_6_out, A, not_5_out, not_6_out);
  and and_7 (and_7_out, A, B, Cin);
  or or_1 (CARRY, and_1_out, and_2_out, and_3_out);
  or or_2 (SUM, and_4_out, and_5_out, and_6_out, and_7_out);
endmodule

module MUX_4X1 (
  input  D0,
  input  D1,
  input  D2,
  input  D3,
  input  S0,
  input  S1,
  output Y
);

  wire and_1_out, and_2_out, and_3_out, and_4_out, not_1_out, not_2_out, not_3_out, not_4_out;

  not not_1 (not_1_out, S0);
  not not_2 (not_2_out, S1);
  not not_3 (not_3_out, S0);
  not not_4 (not_4_out, S1);
  and and_1 (and_1_out, not_1_out, not_2_out, D0);
  and and_2 (and_2_out, not_3_out, S1, D1);
  and and_3 (and_3_out, S0, not_4_out, D2);
  and and_4 (and_4_out, S0, S1, D3);
  or or_1 (Y, and_1_out, and_2_out, and_3_out, and_4_out);
endmodule

module FA_MUX (
  input  A,
  input  B,
  input  in_3,
  input  Cin,
  input  S0,
  input  S1,
  output SUM,
  output CARRY
);

  wire mux_4x1_1_y, not_1_out, not_2_out;

  not not_1 (not_1_out, in_3);
  not not_2 (not_2_out, B);
  MUX_4X1 mux_4x1_1 (.D0(B), .D1(not_2_out), .D2(in_3), .D3(not_1_out), .S0(S0), .S1(S1), .Y(mux_4x1_1_y));
  FA fa_1 (.A(A), .B(mux_4x1_1_y), .Cin(Cin), .SUM(SUM), .CARRY(CARRY));
endmodule

module AU_4_bit (
  input  C_IN,
  input  [3:0] A,
  input  [3:0] B,
  input  [3:0] Constant,
  input  S1,
  input  S0,
  output [3:0] D,
  output Overflow,
  output CarryOut
);

  wire fa_mux_1_carry, fa_mux_2_carry, fa_mux_3_carry;

  FA_MUX fa_mux_1 (
    .A(A[0]), .B(B[0]), .in_3(Constant[0]), .Cin(C_IN), .S0(S1), .SUM(D[0]), .CARRY(fa_mux_1_carry), .S1(S0));
  FA_MUX fa_mux_2 (
    .A(A[1]), .B(B[1]), .in_3(Constant[1]), .Cin(fa_mux_1_carry), .S0(S1), .SUM(D[1]),
    .CARRY(fa_mux_2_carry), .S1(S0));
  FA_MUX fa_mux_3 (
    .A(A[2]), .B(B[2]), .in_3(Constant[2]), .Cin(fa_mux_2_carry), .S0(S1), .SUM(D[2]),
    .CARRY(fa_mux_3_carry), .S1(S0));
  FA_MUX fa_mux_4 (
    .A(A[3]), .B(B[3]), .in_3(Constant[3]), .Cin(fa_mux_3_carry), .S0(S1), .SUM(D[3]), .CARRY(CarryOut),
    .S1(S0));
  xor xor_1 (Overflow, fa_mux_3_carry, CarryOut);

  // Notes on the sheet:
  //   4 Bit AU
endmodule

// Logic
module SSL (
  input  Al,
  input  Bl,
  input  S0,
  input  S1,
  output Logic
);

  wire and_1_out, not_1_out, or_1_out, xor_1_out;

  and and_1 (and_1_out, Al, Bl);
  or or_1 (or_1_out, Al, Bl);
  not not_1 (not_1_out, Al);
  xor xor_1 (xor_1_out, Al, Bl);
  MUX_4X1 mux_4x1_1 (.D0(and_1_out), .D1(or_1_out), .D2(not_1_out), .D3(xor_1_out), .S0(S0), .S1(S1), .Y(Logic));
endmodule

module _4_bit_LU (
  input  [3:0] A,
  input  [3:0] B,
  input  S0,
  input  S1,
  output [3:0] out_5
);

  SSL ssl_1 (.Al(A[0]), .Bl(B[0]), .S0(S0), .Logic(out_5[0]), .S1(S1));
  SSL ssl_2 (.Al(A[1]), .Bl(B[1]), .S0(S0), .Logic(out_5[1]), .S1(S1));
  SSL ssl_3 (.Al(A[2]), .Bl(B[2]), .S0(S0), .Logic(out_5[2]), .S1(S1));
  SSL ssl_4 (.Al(A[3]), .Bl(B[3]), .S0(S0), .Logic(out_5[3]), .S1(S1));
endmodule

module _2X1_MUX (
  input  S0,
  input  D0,
  input  D1,
  output Y
);

  wire and_1_out, and_2_out, not_1_out;

  not not_1 (not_1_out, S0);
  and and_1 (and_1_out, not_1_out, D0);
  and and_2 (and_2_out, S0, D1);
  or or_1 (Y, and_1_out, and_2_out);
endmodule

module Muti_Bit_Mux (
  input  [3:0] A,
  input  [3:0] B,
  input  Select,
  output [3:0] out_4
);

  _2X1_MUX u_2x1_mux_1 (.S0(Select), .D0(A[0]), .D1(B[0]), .Y(out_4[0]));
  _2X1_MUX u_2x1_mux_2 (.S0(Select), .D0(A[1]), .D1(B[1]), .Y(out_4[1]));
  _2X1_MUX u_2x1_mux_3 (.S0(Select), .D0(A[2]), .D1(B[2]), .Y(out_4[2]));
  _2X1_MUX u_2x1_mux_4 (.S0(Select), .D0(A[3]), .D1(B[3]), .Y(out_4[3]));
endmodule
