// Logisim project LAB-5.circ as structural Verilog: 9 circuits, main circuit main
module main (
  input  in_1,
  input  [3:0] B,
  input  [3:0] A,
  input  S2,
  input  S1,
  input  S0,
  input  [3:0] Constant,
  output out_8,
  output [3:0] out_9,
  output out_10
);

  wire [3:0] n4_bit_au_1_d, n4_bit_lu_1_out_5;

  _4_bit_AU u_4_bit_au_1 (
    .A(A), .B(B), .Constant(Constant), .S1(S1), .C_IN(in_1), .D(n4_bit_au_1_d), .Overflow(out_8),
    .CarryOut(out_10), .S0(S0));
  _4_bit_LU u_4_bit_lu_1 (.A(A), .B(B), .S0(S0), .S1(S1), .out_5(n4_bit_lu_1_out_5));
  _2x1_Multbit_MUX_4_bit u_2x1_multbit_mux_4_bit_1 (
    .A(n4_bit_au_1_d), .B(n4_bit_lu_1_out_5), .Select(S2), .out_4(out_9));
endmodule

module Full_Adder (
  input  in_1,
  input  in_2,
  input  in_3
);

  wire and_1_out, and_2_out, or_1_out, xor_1_out, xor_2_out;

  and and_1 (and_1_out, in_2, in_1);
  xor xor_1 (xor_1_out, in_1, in_2);
  or or_1 (or_1_out, and_1_out, and_2_out);
  LED led_1 (.in(or_1_out));
  and and_2 (and_2_out, xor_1_out, in_3);
  xor xor_2 (xor_2_out, xor_1_out, in_3);
  LED led_2 (.in(xor_2_out));

  // Notes on the sheet:
  //   FULL ADDER
endmodule

module MUX_4x1 (
  input  D0,
  input  D1,
  input  D2,
  input  D3,
  input  S0,
  input  S1,
  output Y
);

  wire and_1_out, and_2_out, and_3_out, and_4_out, not_1_out, not_2_out, not_3_out, not_4_out;

  not not_1 (not_1_out, S0);
  not not_2 (not_2_out, S1);
  not not_3 (not_3_out, S0);
  not not_4 (not_4_out, S1);
  and and_1 (and_1_out, not_1_out, not_2_out, D0);
  and and_2 (and_2_out, not_3_out, S1, D1);
  and and_3 (and_3_out, S0, not_4_out, D2);
  and and_4 (and_4_out, S0, S1, D3);
  or or_1 (Y, and_1_out, and_2_out, and_3_out, and_4_out);
endmodule

module Full_Adder___MUX (
  input  A,
  input  B,
  input  in_3,
  input  Cin,
  input  S0,
  input  S1,
  output SUM,
  output CARRY
);

  wire mux_4x1_1_y, not_1_out, not_2_out;

  not not_1 (not_1_out, in_3);
  not not_2 (not_2_out, B);
  MUX_4x1 mux_4x1_1 (.D0(B), .D1(not_2_out), .D2(in_3), .D3(not_1_out), .S0(S0), .S1(S1), .Y(mux_4x1_1_y));
  Full_Adder full_adder_1 (.in_1(A), .in_2(mux_4x1_1_y), .in_3(Cin));
endmodule

module _4_bit_AU (
  input  C_IN,
  input  [3:0] A,
  input  [3:0] B,
  input  [3:0] Constant,
  input  S1,
  input  S0,
  output [3:0] D,
  output Overflow,
  output CarryOut
);

  wire full_adder_mux_1_carry, full_adder_mux_2_carry, full_adder_mux_3_carry;

  Full_Adder___MUX full_adder_mux_1 (
    .A(A[0]), .B(B[0]), .in_3(Constant[0]), .Cin(C_IN), .S0(S1), .SUM(D[0]), .CARRY(full_adder_mux_1_carry),
    .S1(S0));
  Full_Adder___MUX full_adder_mux_2 (
    .A(A[1]), .B(B[1]), .in_3(Constant[1]), .Cin(full_adder_mux_1_carry), .S0(S1), .SUM(D[1]),
    .CARRY(full_adder_mux_2_carry), .S1(S0));
  Full_Adder___MUX full_adder_mux_3 (
    .A(A[2]), .B(B[2]), .in_3(Constant[2]), .Cin(full_adder_mux_2_carry), .S0(S1), .SUM(D[2]),
    .CARRY(full_adder_mux_3_carry), .S1(S0));
  Full_Adder___MUX full_adder_mux_4 (
    .A(A[3]), .B(B[3]), .in_3(Constant[3]), .Cin(full_adder_mux_3_carry), .S0(S1), .SUM(D[3]),
    .CARRY(CarryOut), .S1(S0));
  xor xor_1 (Overflow, full_adder_mux_3_carry, CarryOut);

  // Notes on the sheet:
  //   4 Bit AU
endmodule

module All_Logics (
  input  Al,
  input  Bl,
  input  S0,
  input  S1,
  output Logic
);

  wire and_1_out, not_1_out, or_1_out, xor_1_out;

  and and_1 (and_1_out, Al, Bl);
  or or_1 (or_1_out, Al, Bl);
  not not_1 (not_1_out, Al);
  xor xor_1 (xor_1_out, Al, Bl);
  MUX_4x1 mux_4x1_1 (.D0(and_1_out), .D1(or_1_out), .D2(not_1_out), .D3(xor_1_out), .S0(S0), .S1(S1), .Y(Logic));
endmodule

module _4_bit_LU (
  input  [3:0] A,
  input  [3:0] B,
  input  S0,
  input  S1,
  output [3:0] out_5
);

  All_Logics all_logics_1 (.Al(A[0]), .Bl(B[0]), .S0(S0), .Logic(out_5[0]), .S1(S1));
  All_Logics all_logics_2 (.Al(A[1]), .Bl(B[1]), .S0(S0), .Logic(out_5[1]), .S1(S1));
  All_Logics all_logics_3 (.Al(A[2]), .Bl(B[2]), .S0(S0), .Logic(out_5[2]), .S1(S1));
  All_Logics all_logics_4 (.Al(A[3]), .Bl(B[3]), .S0(S0), .Logic(out_5[3]), .S1(S1));
endmodule

module MUX_2X1 (
  input  S0,
  input  D0,
  input  D1,
  output Y
);

  wire and_1_out, and_2_out, not_1_out;

  not not_1 (not_1_out, S0);
  and and_1 (and_1_out, not_1_out, D0);
  and and_2 (and_2_out, S0, D1);
  or or_1 (Y, and_1_out, and_2_out);
endmodule

module _2x1_Multbit_MUX_4_bit (
  input  [3:0] A,
  input  [3:0] B,
  input  Select,
  output [3:0] out_4
);

  MUX_2X1 mux_2x1_1 (.S0(Select), .D0(A[0]), .D1(B[0]), .Y(out_4[0]));
  MUX_2X1 mux_2x1_2 (.S0(Select), .D0(A[1]), .D1(B[1]), .Y(out_4[1]));
  MUX_2X1 mux_2x1_3 (.S0(Select), .D0(A[2]), .D1(B[2]), .Y(out_4[2]));
  MUX_2X1 mux_2x1_4 (.S0(Select), .D0(A[3]), .D1(B[3]), .Y(out_4[3]));
endmodule
