// Logisim project MY_test.circ as structural Verilog: 1 circuit, main circuit main
module main (
  input  [3:0] A,
  input  [3:0] B,
  input  [3:0] C,
  input  [3:0] D,
  input  [2:0] Selector,
  input  [3:0] A_2,
  input  [3:0] B_2,
  input  [2:0] OP_CODE,
  output [3:0] Output,
  output [3:0] Output_2
);

  wire [3:0] adder_1_out, divider_1_out, multiplier_1_out, subtractor_1_out;

  Adder #(.width(4)) adder_1 (.a(A_2), .b(B_2), .out(adder_1_out));  // open: cin, cout
  Subtractor #(.width(4)) subtractor_1 (.a(A_2), .b(B_2), .out(subtractor_1_out));  // open: bin, bout
  Multiplier #(.width(4)) multiplier_1 (.a(A_2), .b(B_2), .out(multiplier_1_out));  // open: cin, cout
  Divider #(.width(4)) divider_1 (.a(A_2), .b(B_2), .out(divider_1_out));  // open: upper, rem
  Multiplexer #(.select(3), .width(4)) multiplexer_1 (
    .in0(A), .in1(B), .in2(C), .in3(D), .out(Output), .sel(Selector));  // open: in4, in5, in6, in7, en
  Multiplexer #(.select(3), .width(4)) multiplexer_2 (
    .in0(adder_1_out), .in1(subtractor_1_out), .in2(multiplier_1_out), .in3(divider_1_out), .out(Output_2),
    .sel(OP_CODE));  // open: in4, in5, in6, in7, en
endmodule
