// Logisim project LAB -6.circ as structural Verilog
module _1_bit_lu (
  input  in_1,
  input  in_2,
  input  [1:0] select_bit,
  output out_4
);

  wire and_1_out, not_1_out, or_1_out, xor_1_out;

  and and_1 (and_1_out, in_1, in_2);
  or or_1 (or_1_out, in_1, in_2);
  xor xor_1 (xor_1_out, in_1, in_2);
  not not_1 (not_1_out, in_1);
  Multiplexer #(.select(2)) multiplexer_1 (
    .in0(and_1_out), .in1(or_1_out), .in2(xor_1_out), .in3(not_1_out), .out(out_4), .sel(select_bit));  // open: en
endmodule

module _4_bit_lu (
  input  [3:0] in_1,
  input  [1:0] in_2,
  input  [3:0] in_3,
  output [3:0] out_4
);

  _1_bit_lu u_1_bit_lu_1 (.in_1(in_1[0]), .in_2(in_3[0]), .select_bit(in_2), .out_4(out_4[0]));
  _1_bit_lu u_1_bit_lu_2 (.in_1(in_1[1]), .in_2(in_3[1]), .select_bit(in_2), .out_4(out_4[1]));
  _1_bit_lu u_1_bit_lu_3 (.in_1(in_1[2]), .in_2(in_3[2]), .select_bit(in_2), .out_4(out_4[2]));
  _1_bit_lu u_1_bit_lu_4 (.in_1(in_1[3]), .in_2(in_3[3]), .select_bit(in_2), .out_4(out_4[3]));
endmodule

module _4_bit_au (
  input  in_1,
  input  [3:0] in_2,
  input  [3:0] in_3,
  input  [1:0] in_4,
  output [3:0] out_5,
  output carry_out
);

  wire [3:0] multiplexer_1_out, not_1_out;

  assign not_1_out = ~in_3;  // NOT_Gate not_1, 4 bits wide
  Multiplexer #(.select(2), .width(4)) multiplexer_1 (
    .in0(in_3), .in1(not_1_out), .in2(4'b0000), .in3(4'b1111), .out(multiplexer_1_out), .sel(in_4));  // open: en
  Adder #(.width(4)) adder_1 (.a(in_2), .b(multiplexer_1_out), .out(out_5), .cin(in_1), .cout(carry_out));
endmodule

module _4bit_alu (
  input  in_1,
  input  [3:0] in_2,
  input  [1:0] in_3,
  input  in_4,
  input  [3:0] in_5,
  output [3:0] out_6,
  output out_7
);

  wire [3:0] n4_bit_au_1_out_5, n4_bit_lu_1_out_4;

  _4_bit_au u_4_bit_au_1 (
    .in_1(in_1), .in_2(in_2), .in_3(in_5), .in_4(in_3), .out_5(n4_bit_au_1_out_5), .carry_out(out_7));
  _4_bit_lu u_4_bit_lu_1 (.in_1(in_2), .in_2(in_3), .in_3(in_5), .out_4(n4_bit_lu_1_out_4));
  Multiplexer #(.width(4)) multiplexer_1 (
    .in0(n4_bit_au_1_out_5), .in1(n4_bit_lu_1_out_4), .out(out_6), .sel(in_4));  // open: en
endmodule

module ALU_with_register (
  input  in_1,
  input  in_2,
  input  [1:0] in_3,
  input  in_4,
  input  [1:0] in_5,
  input  [1:0] in_6,
  input  [1:0] in_7,
  input  [3:0] in_8,
  output [3:0] out_9,
  output [3:0] out_10,
  output out_11,
  output [3:0] out_12
);

  wire and_1_out, and_2_out, and_3_out, and_4_out, clock_1_out, decoder_1_out0, decoder_1_out1,
       decoder_1_out2, decoder_1_out3;
  wire [3:0] register_1_q, register_2_q, register_3_q, register_4_q;

  Clock clock_1 (.out(clock_1_out));
  Decoder #(.select(2), .enable("false")) decoder_1 (
    .out0(decoder_1_out0), .out1(decoder_1_out1), .out2(decoder_1_out2), .out3(decoder_1_out3), .sel(in_5));
  and and_1 (and_1_out, decoder_1_out0, in_1);
  and and_2 (and_2_out, decoder_1_out1, in_1);
  and and_3 (and_3_out, decoder_1_out2, in_1);
  and and_4 (and_4_out, decoder_1_out3, in_1);
  Register #(.width(4)) register_1 (.D(in_8), .en(and_1_out), .Q(register_1_q), .clk(clock_1_out));  // open: clr
  Register #(.width(4)) register_2 (.D(in_8), .en(and_2_out), .Q(register_2_q), .clk(clock_1_out));  // open: clr
  Register #(.width(4)) register_3 (.D(in_8), .en(and_3_out), .Q(register_3_q), .clk(clock_1_out));  // open: clr
  Register #(.width(4)) register_4 (.D(in_8), .en(and_4_out), .Q(register_4_q), .clk(clock_1_out));  // open: clr
  Multiplexer #(.select(2), .width(4), .disabled(0), .enable("false")) multiplexer_1 (
    .in0(register_1_q), .in1(register_2_q), .in2(register_3_q), .in3(register_4_q), .out(out_9), .sel(in_6));
  Multiplexer #(.select(2), .width(4), .enable("false")) multiplexer_2 (
    .in0(register_1_q), .in1(register_2_q), .in2(register_3_q), .in3(register_4_q), .out(out_12), .sel(in_7));
  _4bit_alu u_4bit_alu_1 (
    .in_1(in_4), .in_2(out_12), .in_3(in_3), .in_4(in_2), .in_5(out_9), .out_6(out_10), .out_7(out_11));
endmodule
