// Logisim project Four_bit_ALU.circ as structural Verilog: 1 circuit, main circuit main
module main (
  input  A,
  input  [3:0] input_1,
  input  [1:0] B,
  input  C,
  input  [3:0] input2,
  output [3:0] ouput,
  output D
);

  wire [3:0] main_1__4_bit_output, main_2__4_bit_output;

  four_bit_AU_main main_1 (
    .in_1(A), .A(input_1), .B(input2), .select_bits(B), ._4_bit_output(main_1__4_bit_output), .Carry_out(D));
  four_bit_LU_main main_2 (
    ._4_bit_A(input_1), ._4_bit_B(input2), ._2_bit_select_lines(B), ._4_bit_output(main_2__4_bit_output));
  Multiplexer #(.width(4)) multiplexer_1 (
    .in0(main_1__4_bit_output), .in1(main_2__4_bit_output), .out(ouput), .sel(C));  // open: en
endmodule
