// Logisim project four_bit_AU.circ as structural Verilog: 1 circuit, main circuit main
module main (
  input  in_1,
  input  [3:0] A,
  input  [3:0] B,
  input  [1:0] select_bits,
  output [3:0] _4_bit_output,
  output Carry_out
);

  wire [3:0] multiplexer_1_out, not_1_out;

  assign not_1_out = ~B;  // NOT_Gate not_1, 4 bits wide
  Multiplexer #(.select(2), .width(4)) multiplexer_1 (
    .in0(B), .in1(not_1_out), .in2(4'b0000), .in3(4'b1111), .out(multiplexer_1_out), .sel(select_bits));  // open: en
  Adder #(.width(4)) adder_1 (.a(A), .b(multiplexer_1_out), .out(_4_bit_output), .cin(in_1), .cout(Carry_out));
endmodule
