// Logisim project four_bit_LU.circ as structural Verilog: 1 circuit, main circuit main
module main (
  input  [3:0] _4_bit_A,
  input  [1:0] _2_bit_select_lines,
  input  [3:0] _4_bit_B,
  output [3:0] _4_bit_output
);

  one_bit_LU_main main_1 (
    .in_1(_4_bit_A[0]), .in_2(_4_bit_B[0]), .select_bit(_2_bit_select_lines), .out_4(_4_bit_output[0]));
  one_bit_LU_main main_2 (
    .in_1(_4_bit_A[1]), .in_2(_4_bit_B[2]), .select_bit(_2_bit_select_lines), .out_4(_4_bit_output[1]));
  one_bit_LU_main main_3 (
    .in_1(_4_bit_A[2]), .in_2(_4_bit_B[2]), .select_bit(_2_bit_select_lines), .out_4(_4_bit_output[2]));
  one_bit_LU_main main_4 (
    .in_1(_4_bit_A[3]), .in_2(_4_bit_B[3]), .select_bit(_2_bit_select_lines), .out_4(_4_bit_output[3]));

  assign _4_bit_B[1] = _4_bit_B[2];
endmodule
